# Fritzing sketch termometro2 (saved by Fritzing 0.9.3b)
breadboards: 1

parts:
  R1 = Resistor [tolerance=±5% resistance=330 package=THT]
  R2 = Resistor [tolerance=±5% resistance=330 package=THT]
  R3 = Resistor [tolerance=±5% resistance=330 package=THT]
  R4 = Resistor [tolerance=±5% resistance=330 package=THT]
  LED2 = smd LED [color="Green (555nm)" package="0603 [SMD]"]
  LED3 = smd LED [color="Blue (430nm)" package="0603 [SMD]"]
  LED4 = smd LED [color="Red (633nm)" package="0603 [SMD]"]
  LED1 = smd LED [color="Yellow (595nm)" package="0805 [SMD]"]
  Componente1 = Arduino Mega 2560 (Rev3)
  R6 = Rotary Potentiometer (Small) [package=THT]
  T2 = LM35 Temperature Sensor [package="TO92 [THT]"]
  U2 = LCD-16X2 BACK [package=lcd-16x2]

nets:
  N1: R1.Pin_0, LED1.anode
  GND: R1.Pin_1, R2.Pin_1, R3.Pin_1, R4.Pin_1, Componente1.GND, R6.gnd, T2.GND, U2.VSS, U2.R_W, U2.K
  N2: R2.Pin_0, LED3.anode
  N3: R3.Pin_0, LED2.anode
  N4: R4.Pin_0, LED4.anode
  N5: LED2.cathode, Componente1.D28
  N6: LED3.cathode, Componente1.D26
  N7: LED4.cathode, Componente1.D32
  N8: LED1.cathode, Componente1.D30
  N9: Componente1.A15, T2.Vout
  5V: Componente1.5V, R6.vcc, T2.+Vs, U2.VDD, U2.A
  N10: Componente1.D43, U2.RS
  N11: Componente1.D45, U2.E
  N12: Componente1.D47, U2.DB4
  N13: Componente1.D49, U2.DB5
  N14: Componente1.D51, U2.DB6
  N15: Componente1.D53, U2.DB7
  N16: R6.out, U2.VO

custom parts:
  Rotary Potentiometer (Small): A rotary adjustable resistor (potentiometer).
  LCD-16X2 BACK: Standard text-only 16x2 parallel input LCD
